// Logisim project Quartz_version_0.circ as structural Verilog: 1 circuit, main circuit main
module main (
);

  wire C_CLOCK, C_PC_ENABLE, C_PC_LATCH;
  wire [7:0] controlled_buffer_1_out, PC_q;
  wire [7:3] pull_resistor_1_node;

  Pull_Resistor pull_resistor_1 (.node({pull_resistor_1_node, C_PC_ENABLE, C_PC_LATCH, C_CLOCK}));
  Register PC (.D(controlled_buffer_1_out), .en(C_PC_LATCH), .clk(C_CLOCK), .Q(PC_q));  // open: clr
  assign controlled_buffer_1_out = C_PC_ENABLE ? PC_q : 8'bz;  // Controlled_Buffer controlled_buffer_1
  Pull_Resistor pull_resistor_2 ();  // open: node
  // Probe on controlled_buffer_1_out
endmodule
